# Fritzing sketch humidifier-water-flow-meter (saved by Fritzing 0.9.2b)
breadboards: 1

parts:
  Part1 = Arduino Uno (Rev3)
  Part2 = Arduino Ethernet Shield (Rev3)
  U1 = LCD-16X2 [package=lcd-16x2]
  R1 = Resistor [tolerance=±1% resistance=3.6k package=THT]
  Reset_Counter_Button = Pushbutton [package="[THT]"]
  R2 = Resistor [tolerance=±1% resistance=10k package=THT]
  Gems_FT-210_Flow_Sensor = mystery part, 3 pins [chip_label=?]
  R3 = Resistor [tolerance=±1% resistance=10k package=THT]
  Display_Button = Pushbutton [package="[THT]"]

nets:
  N1: Part1.D9_PWM, U1.E
  5V: Part2.5V, U1.VDD, Reset_Counter_Button.Pin_1, Reset_Counter_Button.Pin_2, Gems_FT-210_Flow_Sensor.pin2, Display_Button.Pin_1, Display_Button.Pin_2
  N2: Part2.D8, U1.RS
  N3: Part2.A2, Reset_Counter_Button.Pin_3, Reset_Counter_Button.Pin_4, R3.Pin_1
  N4: Part2.A3, R2.Pin_1, Display_Button.Pin_3, Display_Button.Pin_4
  N5: Part2.D2, Gems_FT-210_Flow_Sensor.pin3
  N6: Part2.SDCS, U1.DB4
  N7: Part2.PWM_D5, U1.DB5
  N8: Part2.PWM_D6, U1.DB6
  N9: Part2.D7, U1.DB7
  GND: Part2.GND, U1.VSS, U1.R_W, U1.K, R1.Pin_0, R2.Pin_0, Gems_FT-210_Flow_Sensor.pin1, R3.Pin_0
  N10: U1.VO, R1.Pin_1

// code stored in the sketch: flow-rate-test-1.ino
#include <LiquidCrystal.h>
#include <Ethernet2.h>       // Arduino Ethernet 2 Shield w/ W5500 chip
#include <SPI.h>             // Ethernet Shield communicates w/ Arduino board via SPI bus


const byte flowPin = 2, buttonPin = 3;
const byte lcdLightPin = A5;                // Using analog pin #5 as digital output

volatile unsigned int pulseCounter;
unsigned long lastTimeRead;
unsigned long lastTimeSentData;
float totalGallons;
float flowRate;    // Gallons per minute (GPM)
const float pulseRate = 1386.6666666666666667; // Gems FT-210 flow sensor: 83200 pulses per gallon
                                               // 1 GPM = 1386.666666667 pulses per second

const byte rs=4, en=5, d4=6, d5=7, d6=8, d7=9;
LiquidCrystal lcd(rs, en, d4, d5, d6, d7);
const unsigned int lcdLightOnTime = 10000;   // LCD backlight stays on for 10 seconds with button press
int buttonState = 0;
boolean lcdCheckLightOn;
unsigned int  lcdLightTimer;
unsigned long lcdLightOnStartTime;


byte mac[] = { 0x90, 0xA2, 0xDA, 0x11, 0x15, 0xEF };
EthernetClient netClient;
char serverIP[] = "192.168.101.10";         // Database hosted on remote Prague server


void setup() {
  Ethernet.begin(mac);
  Serial.begin(9600);
  lcd.begin(16, 2);          // LCD display with 16 columns, 2 rows
  lcd.noCursor();            // Hide cursor on LCD display
  lcd.noDisplay();           // Start with LCD display off
  
  pinMode(buttonPin, INPUT);
  pinMode(lcdLightPin, OUTPUT);
  digitalWrite(lcdLightPin, LOW);    // Start with LCD backlight off
  lcdCheckLightOn = false;
  
  pinMode(flowPin, INPUT);
  attachInterrupt(digitalPinToInterrupt(flowPin), detectFlow, FALLING);

  pulseCounter           = 0;
  lastTimeRead           = 0;
  lastTimeSentData       = 0;
  lcdLightTimer          = 0;
  lcdLightOnStartTime    = 0;
  totalGallons           = 0.0;
  flowRate               = 0.0;
}


void loop() {
  buttonState = digitalRead(buttonPin);

  if(buttonState == HIGH) {  // Button pressed
    lcdLightOnStartTime = millis();             // Record the time when button was pressed
    lcdLightTimer = 0;                     
    lcdCheckLightOn = true;
    digitalWrite(lcdLightPin, HIGH);            // Turn on LCD backlight
    lcd.display();                              // Turn on LCD display's text
  }
  else {  // Button not pressed
    if(lcdCheckLightOn) {
      lcdLightTimer = millis() - lcdLightOnStartTime;
      if(lcdLightTimer >= lcdLightOnTime) {
        lcdCheckLightOn = false;
        digitalWrite(lcdLightPin, LOW);         // Turn off LCD backlight
        lcd.noDisplay();                        // Turn off LCD display text
      }
    }
  }
  
  if(millis() - lastTimeRead >= 1000) {
    detachInterrupt(digitalPinToInterrupt(flowPin));  // Disable interrupt during calculations

    // Calculate actual milliseconds since last loop, then scale to a 1 second interval.
    // Divide by sensor's known pulse rate (pulses per second) to get flow rate.
    flowRate = (((1000.0 / (millis() - lastTimeRead)) * pulseCounter) / pulseRate);

    lastTimeRead = millis();                    // Record the time when we went through the loop

    totalGallons += (flowRate / 60);            // Add the volume from this loop to the total volume

    if(millis() - lastTimeSentData >= 30000) {  // Connect and send data to database every 30 seconds
      if(netClient.connect(serverIP, 80)) {
        netClient.print("GET /writedata.php?");
        netClient.print("totalGallons=");
        netClient.print(totalGallons,2);   
        netClient.print("&&");
        netClient.print("flowRate=");
        netClient.print(flowRate,4);
        netClient.println(" HTTP/1.1");
        netClient.println("Host: 192.168.101.10");
        netClient.println("Connection: close");  // End of THIS transmission, not closing net connection
        netClient.println();                     // Blank line
        netClient.println();                     // Blank line
        netClient.stop();                        // Close connection to server
        
        lastTimeSentData = millis();             // Record the time when we sent the data

        // Serial.print("Data sent @ millis = ");
        // Serial.println(lastTimeSentData);
      }
      else {
        // Serial.println("\n*** Connection Failed! ***\n");
      }
    }

  /*
    Serial.print(flowRate,4);           // Print flow rate to 4 decimal places
    Serial.println(" GPM");
    Serial.print(totalGallons,2);       // Print total cumulative volume (gallons)
    Serial.println(" Total Gallons");
  */
  
    lcd.clear();
    lcd.setCursor(3, 0);                // Cursor to 4th column, 1st row
    lcd.print(flowRate,4);              // Print flow rate to 4 decimal places
    lcd.print(" GPM");
    lcd.setCursor(2, 1);                // Cursor to 3rd column, 2nd row
    lcd.print(totalGallons,2);          // Print total cumulative volume (gallons)
    lcd.print(" Gallons");

    pulseCounter = 0;                   // Reset counter each loop

    attachInterrupt(digitalPinToInterrupt(flowPin), detectFlow, FALLING);  // Re-enable interrupt
  }
}


void detectFlow() {
   pulseCounter++;
}
